# Fritzing sketch ArduinoAntennaSwitch - Relay (saved by Fritzing 0.9.3b)
breadboards: 1

parts:
  Q1 = TRANSISTOR_NPN [package=to-92-ammo]
  U2 = RELAY [package=OJ]
  R1 = Resistor [tolerance=±5% resistance=220 package="2010 [SMD]"]
  D2 = Diode [package=diode-1n4001]

nets:
  N1: Q1.B, R1.Pin_0
  N2: U2.COIL2, U2.NO, D2.A, D2.C

notes:
  From Decoder
  6/9/12VDC
  Ground
  Antenna- Coax core
