# Fritzing sketch ArduinoAntennaSwitch (saved by Fritzing 0.9.2b)
breadboards: 1

parts:
  Part1 = Arduino Uno (Rev3) - ICSP
  U2 = M74HC238 [package=dil16]
  SW1 = ENCODER_RGB_CA [package=encoder_led_3]
  LCD1 = LCD screen
  LED1 = smd LED [color="Red (633nm)" package="0805 [SMD]"]
  LED2 = smd LED [color="Green (555nm)" package="0805 [SMD]"]
  R1 = Resistor [tolerance=±5% resistance=220 package="1206 [SMD]"]
  S2 = Round Pushbutton

nets:
  N1: Part1.A4/SDA, LCD1.VDD
  N2: Part1.A5/SCL, LCD1.VSS
  GND: Part1.GND, U2.~G2A, U2.~G2B, U2.GND, SW1.-R, LCD1.LED+, R1.Pin_0, S2.leg1
  N3: Part1.D10_PWM/SS, SW1.SW
  N4: Part1.D11_PWM/MOSI, SW1.-G
  N5: Part1.D12/MISO, LED1.anode
  N6: Part1.D13/SCK, LED2.anode
  N7: Part1.D2, S2.leg0
  N8: Part1.D3_PWM, SW1.-B
  N9: Part1.D4, U2.A
  N10: Part1.D5_PWM, U2.B
  N11: Part1.D6_PWM, U2.C
  5V: Part1.5V, U2.G1, U2.VCC, SW1.C
  N12: U2.Y3, U2.Y2, U2.Y1, U2.Y0
  N13: LED1.cathode, LED2.cathode, R1.Pin_1

notes:
  Toggle switch.
  Toggles between
  "Radio Priority Mode"
  and
  "Manual Only Mode"
  Rotary Encoder. Manual antenna selection
  LCD -
  I2C communication
  3 to 8 decoder.
  Gets a 3bit code from the arduino and selects 1 of the 8 relays(Does not show here)
  To Relay Array
  Auto/Manual mode LED's
  To Radio (RS232)
